# Fritzing sketch Lamp+TM1637+DFplayer (saved by Fritzing 0.9.3b)

parts:
  WeMos_D1_Mini1 = WeMos D1 Mini
  TM1637 = TM1637 Display
  TP1 = TTP223 Touch Module [part_number=TTP223]
  R1 = Resistor [tolerance=±5% resistance=220 package="0805 [SMD]"]
  R2 = Resistor [tolerance=±5% resistance=220 package="0805 [SMD]"]
  R3 = Resistor [tolerance=±5% resistance=100k package="0805 [SMD]"]
  Power_5_5x2_1 = Power 5.5x2.5
  Часть1 = NeoPixel NeoMatrix 8x8 [part_number=1487]
  Q3 = Basic FET N-Channel [package="TO220 [THT]"]
  D1 = Schottky Diode [part_number=1N5817 package="300 mil [THT]"]
  C1_470_0 = Capacitor Polarized [package=cpol-radial-10uf-25v]
  DFPlayer_Mini1 = DFPlayer MINI [package="DIP (Dual Inline) [THT]"]
  SP1 = SPEAKER [package=pcb_mount_speaker]

nets:
  3V3: WeMos_D1_Mini1.3V3, TP1.VCC
  N1: WeMos_D1_Mini1.5V, D1.cathode
  N2: WeMos_D1_Mini1.D0, TM1637.pin2
  N3: WeMos_D1_Mini1.D1, R1.Pin_0
  N4: WeMos_D1_Mini1.D2, TP1.I/O
  N5: WeMos_D1_Mini1.D3, R2.Pin_0
  N6: WeMos_D1_Mini1.D5, TM1637.pin1
  N7: WeMos_D1_Mini1.D7, DFPlayer_Mini1.TX
  N8: WeMos_D1_Mini1.D8, DFPlayer_Mini1.RX
  N9: WeMos_D1_Mini1.G, TM1637.pin4, R3.Pin_1, Power_5_5x2_1.GND, Q3.source, C1_470_0.-
  N10: TM1637.pin3, C1_470_0.+, DFPlayer_Mini1.VCC
  GND: TP1.GND, DFPlayer_Mini1.GND
  N11: R1.Pin_1, R3.Pin_0, Q3.gate
  N12: R2.Pin_1, Часть1.IN
  N13: Power_5_5x2_1.PWR, Часть1.VDD, D1.anode
  N14: Часть1.GND, Q3.drain
  N15: DFPlayer_Mini1.SPK1, SP1.-
  N16: DFPlayer_Mini1.SPK2, SP1.+

custom parts:
  TTP223 Touch Module: Single touch module. Other side has "A" "B" terminal to short and use "AHLB" & "Toggle" Mode.
  NeoPixel NeoMatrix 8x8: Put on your sunglasses before wiring up this LED matrix - 64 eye-blistering RGB LEDs adorn the NeoMatrix for a blast of configurable color. Arranged in an 8x8 matrix, each pixel is individually addressable. Only one microcontroller pin is required to control all the LEDs, and you get 24 bit color for each LED.
  DFPlayer MINI: MP3 module by DFRobot.com for playing Music from an SD-Card. Supports WAV and MP3 files.
